// Logisim project 1G07.circ as structural Verilog: 1 circuit, main circuit main
module main (
  input  in_1,
  input  in_2,
  input  in_3,
  input  in_4
);

  wire and_1_out, multiplexer_1_out, nand_1_out, undriven;

  nand nand_1 (nand_1_out, in_1, in_1);
  and and_1 (and_1_out, in_1, in_1);
  Multiplexer #(.enable("false")) multiplexer_1 (
    .in0(nand_1_out), .in1(and_1_out), .out(multiplexer_1_out), .sel(undriven));

  assign in_3 = in_1;
endmodule
