// Logisim project 3G07.circ as structural Verilog: 1 circuit, main circuit main
module main (
  input  in_1,
  input  in_2,
  input  in_3,
  input  in_4,
  input  in_5,
  input  in_6
);

  wire and_1_out, and_2_out, nand_1_out, nand_2_out, nor_1_out, or_2_out;

  nand nand_1 (nand_1_out, in_1, in_2);
  nand nand_2 (nand_2_out, in_1, in_2);
  not not_1 (in_6, nor_1_out);
  nor nor_1 (nor_1_out, in_3, in_4);
  and and_1 (and_1_out, in_3, in_4);
  and and_2 (and_2_out, nand_1_out, nand_2_out);
  or or_1 (and_2_out, nor_1_out, and_1_out);
  or or_2 (or_2_out, and_1_out, and_1_out);
  and and_3 (in_5, and_2_out, or_2_out);
endmodule
