// Logisim project 4G07.circ as structural Verilog: 1 circuit, main circuit main
module main (
  input  in_1,
  input  in_2,
  input  in_3,
  input  in_4,
  input  in_5,
  input  in_6,
  input  in_7
);

  wire and_1_out, and_2_out, and_3_out, and_4_out, nor_1_out, not_1_out, not_2_out, not_3_out, not_4_out,
       or_1_out, or_2_out, xnor_1_out, xor_1_out;

  xor xor_1 (xor_1_out, in_1, in_3);
  xnor xnor_1 (xnor_1_out, in_1, in_3);
  or or_1 (or_1_out, in_4, in_5);
  nor nor_1 (nor_1_out, in_4, in_5);
  not not_1 (not_1_out, in_7);
  not not_2 (not_2_out, in_7);
  not not_3 (not_3_out, in_7);
  not not_4 (not_4_out, in_7);
  and and_1 (and_1_out, xor_1_out, not_1_out);
  and and_2 (and_2_out, xnor_1_out, not_3_out);
  and and_3 (and_3_out, or_1_out, in_7);
  and and_4 (and_4_out, in_7, nor_1_out);
  or or_2 (or_2_out, and_2_out, and_4_out);
endmodule
