// Logisim project 5G07.circ as structural Verilog: 1 circuit, main circuit main
module main (
  input  in_1,
  input  in_2,
  input  in_3,
  input  in_4,
  input  in_5
);

  wire or_1_out, or_2_out, xor_1_out;

  xor xor_1 (xor_1_out, in_1, in_2);
  or or_1 (or_1_out, in_1, in_2);
  or or_2 (or_2_out, in_3, in_5);
  // NOR_Gate nor_1 has open pins: in0=in_3, in1=in_5, out=open
  Multiplexer #(.enable("false")) multiplexer_1 (.in0(xor_1_out), .in1(or_1_out), .out(in_4), .sel(or_2_out));
endmodule
