// Logisim project 2G08.circ as structural Verilog: 1 circuit, main circuit main
module main (
  input  in_1,
  input  in_2,
  input  in_3,
  input  in_4,
  input  in_5
);

  wire and_1_out, and_2_out, and_3_out, and_4_out, not_1_out, not_2_out, not_3_out, or_1_out, or_2_out,
       or_3_out, or_4_out;

  not not_1 (not_1_out, in_1);
  not not_2 (not_2_out, in_2);
  not not_3 (not_3_out, in_3);
  buf or_1 (or_1_out, in_5);  // OR_Gate
  and and_1 (and_1_out, not_1_out, in_1);
  and and_2 (and_2_out, not_2_out, in_2);
  and and_3 (and_3_out, not_3_out, in_2);
  and and_4 (and_4_out, or_1_out, in_2);
  or or_2 (or_2_out, and_1_out, and_2_out);
  or or_3 (or_3_out, or_2_out, or_2_out);
  or or_4 (or_4_out, and_3_out, and_4_out);
  and and_5 (in_4, or_3_out, or_4_out);
endmodule
