// Logisim project Circuitos11.circ as structural Verilog
module G1101 (
  input  in_1,
  input  in_2,
  output S_moore,
  output S_mealy
);

  wire clock_1_out, d_ff_2_q, d_ff_4_q, d_ff_5_q;

  Clock clock_1 (.out(clock_1_out));
  D_Flip_Flop #(.Pre_Clr_Positions("LEGACY"), .enable("true"), .NewFFLayout("false")) d_ff_1 (
    .clk(clock_1_out), .Q(in_2), .preset(in_1), .reset(in_2));  // open: D, Qn, en
  and and_1 (S_mealy, in_2, in_2, in_2, in_2);
  D_Flip_Flop #(.Pre_Clr_Positions("LEGACY"), .enable("true"), .NewFFLayout("false")) d_ff_2 (
    .clk(clock_1_out), .Q(d_ff_2_q), .preset(in_2), .en(in_2), .reset(in_2));  // open: D, Qn
  D_Flip_Flop #(.Pre_Clr_Positions("LEGACY"), .enable("true"), .NewFFLayout("false")) d_ff_3 (
    .clk(clock_1_out), .Q(S_moore), .preset(S_mealy));  // open: D, Qn, en, reset
  D_Flip_Flop #(.Pre_Clr_Positions("LEGACY"), .enable("true"), .NewFFLayout("false")) d_ff_4 (
    .clk(clock_1_out), .Q(d_ff_4_q), .preset(d_ff_2_q), .en(in_2), .reset(d_ff_4_q));  // open: D, Qn
  D_Flip_Flop #(.Pre_Clr_Positions("LEGACY"), .enable("true"), .NewFFLayout("false")) d_ff_5 (
    .clk(clock_1_out), .Q(d_ff_5_q), .preset(d_ff_4_q), .reset(in_2));  // open: D, Qn, en
endmodule

module G1103 (
  input  x,
  input  Reset,
  output [7:0] out_3,
  output out_4
);

  wire and_1_out, and_2_out, clock_1_out, d_ff_1_q, d_ff_2_q, d_ff_2_qn, d_ff_3_q, d_ff_4_q, d_ff_4_qn,
       not_1_out, or_1_out;

  Clock clock_1 (.out(clock_1_out));
  or or_1 (or_1_out, Reset, Reset, and_1_out);
  D_Flip_Flop #(.Pre_Clr_Positions("LEGACY"), .enable("true"), .NewFFLayout("false")) d_ff_1 (
    .clk(clock_1_out), .D(x), .Q(d_ff_1_q), .reset(or_1_out));  // open: Qn, preset, en
  and and_1 (and_1_out, d_ff_4_q, out_4);
  and and_2 (and_2_out, out_4, not_1_out);
  not not_1 (not_1_out, clock_1_out);
  D_Flip_Flop #(.Pre_Clr_Positions("LEGACY"), .enable("true"), .NewFFLayout("false")) d_ff_2 (
    .clk(clock_1_out), .Q(d_ff_2_q), .Qn(d_ff_2_qn), .reset(Reset));  // open: D, preset, en
  and and_3 (out_4, d_ff_1_q, d_ff_2_qn, d_ff_3_q, d_ff_4_qn);
  D_Flip_Flop #(.Pre_Clr_Positions("LEGACY"), .enable("true"), .NewFFLayout("false")) d_ff_3 (
    .clk(clock_1_out), .D(d_ff_2_q), .Q(d_ff_3_q), .reset(Reset));  // open: Qn, preset, en
  D_Flip_Flop #(.Pre_Clr_Positions("LEGACY"), .enable("true"), .NewFFLayout("false")) d_ff_4 (
    .clk(clock_1_out), .Q(d_ff_4_q), .Qn(d_ff_4_qn), .reset(Reset));  // open: D, preset, en
  Counter #(.behavior("old")) counter_1 (
    .count(out_4), .Q(out_3), .clk(and_2_out), .clr(Reset));  // open: load, D, carry, preset

  // Notes on the sheet:
  //   MOORE E MEALY
  //   Contador
endmodule

module G1104 (
  input  in_1,
  input  Reset,
  output out_3
);

  wire and_1_out, clock_1_out, d_ff_1_q, d_ff_1_qn, d_ff_2_q, d_ff_3_q, d_ff_3_qn, not_1_out, or_1_out;
  wire [1:0] counter_1_q;

  Clock clock_1 (.out(clock_1_out));
  D_Flip_Flop #(.Pre_Clr_Positions("LEGACY"), .enable("true"), .NewFFLayout("false")) d_ff_1 (
    .clk(clock_1_out), .D(in_1), .Q(d_ff_1_q), .Qn(d_ff_1_qn), .reset(or_1_out));  // open: preset, en
  or or_1 (or_1_out, counter_1_q[0], Reset);
  not not_1 (not_1_out, clock_1_out);
  D_Flip_Flop #(.Pre_Clr_Positions("LEGACY"), .enable("true"), .NewFFLayout("false")) d_ff_2 (
    .clk(clock_1_out), .D(d_ff_1_q), .Q(d_ff_2_q), .reset(or_1_out));  // open: Qn, preset, en
  and and_1 (and_1_out, out_3, out_3, not_1_out);
  and and_2 (out_3, d_ff_1_qn, d_ff_2_q, d_ff_3_qn, Reset);
  D_Flip_Flop #(.Pre_Clr_Positions("LEGACY"), .enable("true"), .NewFFLayout("false")) d_ff_3 (
    .clk(clock_1_out), .D(d_ff_2_q), .Q(d_ff_3_q), .Qn(d_ff_3_qn), .reset(or_1_out));  // open: preset, en
  D_Flip_Flop #(.Pre_Clr_Positions("LEGACY"), .enable("true"), .NewFFLayout("false")) d_ff_4 (
    .clk(clock_1_out), .D(d_ff_3_q), .Q(Reset), .reset(or_1_out));  // open: Qn, preset, en
  Counter #(.width(2), .max('h3), .behavior("old")) counter_1 (
    .count(out_3), .Q(counter_1_q), .clk(and_1_out), .clr(Reset));  // open: load, D, carry, preset

  // Notes on the sheet:
  //   ESTADO FINITO 
  //   Contador
endmodule

module G1105 (
  input  in_1,
  input  Reset,
  output [7:0] out_3,
  output out_4
);

  wire and_1_out, and_2_out, clock_1_out, d_ff_1_q, d_ff_2_q, d_ff_2_qn, d_ff_3_q, d_ff_4_q, d_ff_4_qn,
       not_1_out, or_1_out;

  Clock clock_1 (.out(clock_1_out));
  or or_1 (or_1_out, Reset, Reset, and_1_out);
  D_Flip_Flop #(.Pre_Clr_Positions("LEGACY"), .enable("true"), .NewFFLayout("false")) d_ff_1 (
    .clk(clock_1_out), .D(in_1), .Q(d_ff_1_q), .reset(or_1_out));  // open: Qn, preset, en
  and and_1 (and_1_out, d_ff_4_q, out_4);
  buf and_2 (and_2_out, not_1_out);  // AND_Gate
  not not_1 (not_1_out, clock_1_out);
  D_Flip_Flop #(.Pre_Clr_Positions("LEGACY"), .enable("true"), .NewFFLayout("false")) d_ff_2 (
    .clk(clock_1_out), .Q(d_ff_2_q), .Qn(d_ff_2_qn), .reset(Reset));  // open: D, preset, en
  and and_3 (out_4, d_ff_1_q, d_ff_2_qn, d_ff_3_q, d_ff_4_qn);
  D_Flip_Flop #(.Pre_Clr_Positions("LEGACY"), .enable("true"), .NewFFLayout("false")) d_ff_3 (
    .clk(clock_1_out), .D(d_ff_2_q), .Q(d_ff_3_q), .reset(Reset));  // open: Qn, preset, en
  D_Flip_Flop #(.Pre_Clr_Positions("LEGACY"), .enable("true"), .NewFFLayout("false")) d_ff_4 (
    .clk(clock_1_out), .Q(d_ff_4_q), .Qn(d_ff_4_qn), .reset(Reset));  // open: D, preset, en
  Counter #(.behavior("old")) counter_1 (
    .count(out_4), .Q(out_3), .clk(and_2_out), .clr(Reset));  // open: load, D, carry, preset

  // Notes on the sheet:
  //   SEM INCERÇÃO
  //   Contador
endmodule

module G1106 (
  input  in_1,
  input  Reset,
  output [7:0] out_3,
  output out_4
);

  wire and_1_out, and_2_out, clock_1_out, d_ff_1_q, d_ff_2_q, d_ff_2_qn, d_ff_3_q, d_ff_4_q, d_ff_4_qn,
       not_1_out, or_1_out;

  Clock clock_1 (.out(clock_1_out));
  or or_1 (or_1_out, Reset, Reset, and_1_out);
  D_Flip_Flop #(.Pre_Clr_Positions("LEGACY"), .enable("true"), .NewFFLayout("false")) d_ff_1 (
    .clk(clock_1_out), .D(in_1), .Q(d_ff_1_q), .reset(or_1_out));  // open: Qn, preset, en
  and and_1 (and_1_out, d_ff_4_q, out_4);
  and and_2 (and_2_out, out_4, not_1_out);
  not not_1 (not_1_out, clock_1_out);
  D_Flip_Flop #(.Pre_Clr_Positions("LEGACY"), .enable("true"), .NewFFLayout("false")) d_ff_2 (
    .clk(clock_1_out), .Q(d_ff_2_q), .Qn(d_ff_2_qn), .reset(Reset));  // open: D, preset, en
  and and_3 (out_4, d_ff_1_q, d_ff_2_qn, d_ff_3_q, d_ff_4_qn);
  D_Flip_Flop #(.Pre_Clr_Positions("LEGACY"), .enable("true"), .NewFFLayout("false")) d_ff_3 (
    .clk(clock_1_out), .D(d_ff_2_q), .Q(d_ff_3_q), .reset(Reset));  // open: Qn, preset, en
  D_Flip_Flop #(.Pre_Clr_Positions("LEGACY"), .enable("true"), .NewFFLayout("false")) d_ff_4 (
    .clk(clock_1_out), .Q(d_ff_4_q), .Qn(d_ff_4_qn), .reset(Reset));  // open: D, preset, en
  Counter #(.behavior("old")) counter_1 (
    .count(out_4), .Q(out_3), .clk(and_2_out), .clr(Reset));  // open: load, D, carry, preset

  // Notes on the sheet:
  //   COM INSERÇÃO
  //   Contador
endmodule
