// Logisim project Exercicio_1401.circ as structural Verilog: 1 circuit, main circuit Exemplo 1
module Exemplo_1 (
  input  Clk,
  input  in,
  input  Clr,
  output out_4,
  output out_5,
  output out_6,
  output out_7,
  output out_8
);

  D_Flip_Flop #(.Pre_Clr_Positions("LEGACY"), .enable("true"), .NewFFLayout("false")) d_ff_1 (
    .clk(Clk), .Q(out_4));  // open: D, Qn, preset, en, reset
  D_Flip_Flop #(.Pre_Clr_Positions("LEGACY"), .enable("true"), .NewFFLayout("false")) d_ff_2 (
    .clk(Clk), .Q(Clr));  // open: D, Qn, preset, en, reset
  D_Flip_Flop #(.Pre_Clr_Positions("LEGACY"), .enable("true"), .NewFFLayout("false")) d_ff_3 (
    .clk(Clk), .Q(Clr));  // open: D, Qn, preset, en, reset
  D_Flip_Flop #(.Pre_Clr_Positions("LEGACY"), .enable("true"), .NewFFLayout("false")) d_ff_4 (
    .clk(Clk), .Q(Clr));  // open: D, Qn, preset, en, reset
  D_Flip_Flop #(.Pre_Clr_Positions("LEGACY"), .enable("true"), .NewFFLayout("false")) d_ff_5 (
    .clk(Clk), .D(in), .Q(Clr), .preset(Clr));  // open: Qn, en, reset

  assign out_5 = Clr;
  assign out_6 = Clr;
  assign out_7 = Clr;
  assign out_8 = Clr;
endmodule
