// Logisim project Exercicio_1402.circ as structural Verilog: 1 circuit, main circuit main
module main (
  input  Clk,
  input  Clr,
  input  Load,
  input  in_4,
  input  in_5,
  input  in_6,
  input  in_7,
  input  in_8,
  output out_9,
  output out_10,
  output out_11,
  output out_12,
  output out_13
);

  wire and_5_out;

  D_Flip_Flop #(.Pre_Clr_Positions("LEGACY"), .enable("true"), .NewFFLayout("false")) d_ff_1 (
    .clk(Clk), .Q(out_9), .en(Clr));  // open: D, Qn, preset, reset
  and and_1 (out_10, in_4, in_4, in_4, in_4, in_4);
  and and_2 (out_11, in_4, in_4, in_4, in_4, in_4);
  D_Flip_Flop #(.Pre_Clr_Positions("LEGACY"), .enable("true"), .NewFFLayout("false")) d_ff_2 (
    .clk(Clk), .Q(out_10), .preset(Clr), .en(Clr));  // open: D, Qn, reset
  D_Flip_Flop #(.Pre_Clr_Positions("LEGACY"), .enable("true"), .NewFFLayout("false")) d_ff_3 (
    .clk(Clk), .Q(out_11), .en(Clr));  // open: D, Qn, preset, reset
  and and_3 (out_12, in_4, in_4, in_4, in_4, in_4);
  D_Flip_Flop #(.Pre_Clr_Positions("LEGACY"), .enable("true"), .NewFFLayout("false")) d_ff_4 (
    .clk(Clk), .Q(out_12), .en(Clr));  // open: D, Qn, preset, reset
  and and_4 (out_13, in_4, in_4, in_4, in_4, in_4);
  and and_5 (and_5_out, in_4, in_4, in_4, in_4);
  D_Flip_Flop #(.Pre_Clr_Positions("LEGACY"), .enable("true"), .NewFFLayout("false")) d_ff_5 (
    .clk(Clk), .D(1'b0), .Q(out_13), .preset(Clr), .en(Clr));  // open: Qn, reset

  assign in_5 = in_4;
  assign in_6 = in_4;
  assign in_7 = in_4;
  assign in_8 = in_4;
  assign Load = in_4;
endmodule
