// Logisim project Exercicio_1403.circ as structural Verilog: 1 circuit, main circuit main
module main (
  input  Clk,
  input  in,
  input  Clr,
  output out_4,
  output out_5,
  output out_6,
  output out_7,
  output out_8
);

  wire or_1_out;

  buf or_1 (or_1_out, in);  // OR_Gate
  D_Flip_Flop #(.Pre_Clr_Positions("LEGACY"), .enable("true"), .NewFFLayout("false")) d_ff_1 (
    .clk(Clk), .D(or_1_out), .Q(Clr), .preset(Clr));  // open: Qn, en, reset
  D_Flip_Flop #(.Pre_Clr_Positions("LEGACY"), .enable("true"), .NewFFLayout("false")) d_ff_2 (
    .clk(Clk), .Q(Clr));  // open: D, Qn, preset, en, reset
  D_Flip_Flop #(.Pre_Clr_Positions("LEGACY"), .enable("true"), .NewFFLayout("false")) d_ff_3 (
    .clk(Clk), .Q(Clr));  // open: D, Qn, preset, en, reset
  D_Flip_Flop #(.Pre_Clr_Positions("LEGACY"), .enable("true"), .NewFFLayout("false")) d_ff_4 (
    .clk(Clk), .D(Clk), .Q(Clr));  // open: Qn, preset, en, reset
  D_Flip_Flop #(.Pre_Clr_Positions("LEGACY"), .enable("true"), .NewFFLayout("false")) d_ff_5 (
    .clk(Clk), .Q(out_8), .preset(Clr));  // open: D, Qn, en, reset

  assign out_4 = Clr;
  assign out_5 = Clr;
  assign out_6 = Clr;
  assign out_7 = Clr;
endmodule
