// Logisim project Exercicio_1405.circ as structural Verilog: 1 circuit, main circuit main
module main (
  input  Clk,
  input  Clr,
  input  Load,
  input  in_4,
  input  in_5,
  input  in_6,
  input  in_7,
  input  in_8,
  output out_9,
  output out_10,
  output out_11,
  output out_12,
  output out_13
);

  wire and_1_out, undriven;

  and and_1 (and_1_out, in_4, in_4, in_4, in_4, in_4);
  D_Flip_Flop #(.Pre_Clr_Positions("LEGACY"), .enable("true"), .NewFFLayout("false")) d_ff_1 (
    .clk(Clk), .Q(out_9), .en(Clr));  // open: D, Qn, preset, reset
  and and_2 (out_9, in_4, in_4, in_4, in_4, in_4);
  D_Flip_Flop #(.Pre_Clr_Positions("LEGACY"), .enable("true"), .NewFFLayout("false")) d_ff_2 (
    .clk(Clk), .Q(out_10), .en(Clr));  // open: D, Qn, preset, reset
  D_Flip_Flop #(.Pre_Clr_Positions("LEGACY"), .enable("true"), .NewFFLayout("false")) d_ff_3 (
    .clk(Clk), .Q(out_11), .preset(undriven), .en(Clr));  // open: D, Qn, reset
  and and_3 (out_10, in_4, in_4, in_4, in_4, in_4);
  and and_4 (out_11, in_4, in_4, in_4, in_4, in_4);
  D_Flip_Flop #(.Pre_Clr_Positions("LEGACY"), .enable("true"), .NewFFLayout("false")) d_ff_4 (
    .clk(Clk), .Q(out_12), .preset(Clr), .en(Clr));  // open: D, Qn, reset
  D_Flip_Flop #(.Pre_Clr_Positions("LEGACY"), .enable("true"), .NewFFLayout("false")) d_ff_5 (
    .clk(Clk), .Q(out_13), .preset(Clr), .en(Clr));  // open: D, Qn, reset
  and and_5 (out_12, in_4, in_4, in_4, in_4);

  assign in_5 = in_4;
  assign in_6 = in_4;
  assign in_7 = in_4;
  assign in_8 = in_4;
  assign Load = in_4;
  // also tied to GND on the sheet: and_1_out
endmodule
